// Digital circuit 1X15 SRAM.dig as structural Verilog
module _1X15_SRAM (
  input  RS1,
  input  RS2,
  input  WS,
  input  [14:0] WD_14_0,
  input  CLK,
  output [14:0] RD1_14_0,
  output [14:0] RD2_14_0
);

  _1X1_SRAM _1x1_sram_1 (
    .WD(WD_14_0[0]), .WS(WS), .Clk(CLK), .RS1(RS1), .RS2(RS2), .RD1(RD1_14_0[0]), .RD2(RD2_14_0[0]));
  _1X1_SRAM _1x1_sram_2 (
    .WD(WD_14_0[3]), .WS(WS), .Clk(CLK), .RS1(RS1), .RS2(RS2), .RD1(RD1_14_0[3]), .RD2(RD2_14_0[3]));
  _1X1_SRAM _1x1_sram_3 (
    .WD(WD_14_0[6]), .WS(WS), .Clk(CLK), .RS1(RS1), .RS2(RS2), .RD1(RD1_14_0[6]), .RD2(RD2_14_0[6]));
  _1X1_SRAM _1x1_sram_4 (
    .WD(WD_14_0[9]), .WS(WS), .Clk(CLK), .RS1(RS1), .RS2(RS2), .RD1(RD1_14_0[9]), .RD2(RD2_14_0[9]));
  _1X1_SRAM _1x1_sram_5 (
    .WD(WD_14_0[12]), .WS(WS), .Clk(CLK), .RS1(RS1), .RS2(RS2), .RD1(RD1_14_0[12]), .RD2(RD2_14_0[12]));
  _1X1_SRAM _1x1_sram_6 (
    .WD(WD_14_0[1]), .WS(WS), .Clk(CLK), .RS1(RS1), .RS2(RS2), .RD1(RD1_14_0[1]), .RD2(RD2_14_0[1]));
  _1X1_SRAM _1x1_sram_7 (
    .WD(WD_14_0[4]), .WS(WS), .Clk(CLK), .RS1(RS1), .RS2(RS2), .RD1(RD1_14_0[4]), .RD2(RD2_14_0[4]));
  _1X1_SRAM _1x1_sram_8 (
    .WD(WD_14_0[7]), .WS(WS), .Clk(CLK), .RS1(RS1), .RS2(RS2), .RD1(RD1_14_0[7]), .RD2(RD2_14_0[7]));
  _1X1_SRAM _1x1_sram_9 (
    .WD(WD_14_0[10]), .WS(WS), .Clk(CLK), .RS1(RS1), .RS2(RS2), .RD1(RD1_14_0[10]), .RD2(RD2_14_0[10]));
  _1X1_SRAM _1x1_sram_10 (
    .WD(WD_14_0[13]), .WS(WS), .Clk(CLK), .RS1(RS1), .RS2(RS2), .RD1(RD1_14_0[13]), .RD2(RD2_14_0[13]));
  _1X1_SRAM _1x1_sram_11 (
    .WD(WD_14_0[2]), .WS(WS), .Clk(CLK), .RS1(RS1), .RS2(RS2), .RD1(RD1_14_0[2]), .RD2(RD2_14_0[2]));
  _1X1_SRAM _1x1_sram_12 (
    .WD(WD_14_0[5]), .WS(WS), .Clk(CLK), .RS1(RS1), .RS2(RS2), .RD1(RD1_14_0[5]), .RD2(RD2_14_0[5]));
  _1X1_SRAM _1x1_sram_13 (
    .WD(WD_14_0[8]), .WS(WS), .Clk(CLK), .RS1(RS1), .RS2(RS2), .RD1(RD1_14_0[8]), .RD2(RD2_14_0[8]));
  _1X1_SRAM _1x1_sram_14 (
    .WD(WD_14_0[11]), .WS(WS), .Clk(CLK), .RS1(RS1), .RS2(RS2), .RD1(RD1_14_0[11]), .RD2(RD2_14_0[11]));
  _1X1_SRAM _1x1_sram_15 (
    .WD(WD_14_0[14]), .WS(WS), .Clk(CLK), .RS1(RS1), .RS2(RS2), .RD1(RD1_14_0[14]), .RD2(RD2_14_0[14]));

  // Other names for the same wires on the sheet: RDi0 = RD1_14_0[0]; RDi1 = RD1_14_0[1]; RDi2 = RD1_14_0[2];
  //   RDi3 = RD1_14_0[3]; RDi4 = RD1_14_0[4]; RDi5 = RD1_14_0[5]; RDi6 = RD1_14_0[6]; RDi7 = RD1_14_0[7];
  //   RDi8 = RD1_14_0[8]; RDi9 = RD1_14_0[9]; RDi10 = RD1_14_0[10]; RDi11 = RD1_14_0[11]; RDi12 = RD1_14_0[12];
  //   RDi13 = RD1_14_0[13]; RDi14 = RD1_14_0[14]; RDii0 = RD2_14_0[0]; RDii1 = RD2_14_0[1]; RDii2 = RD2_14_0[2];
  //   RDii3 = RD2_14_0[3]; RDii4 = RD2_14_0[4]; RDii5 = RD2_14_0[5]; RDii6 = RD2_14_0[6]; RDii7 = RD2_14_0[7];
  //   RDii8 = RD2_14_0[8]; RDii9 = RD2_14_0[9]; RDii10 = RD2_14_0[10]; RDii11 = RD2_14_0[11]; RDii12 = RD2_14_0[12];
  //   RDii13 = RD2_14_0[13]; RDii14 = RD2_14_0[14]; WD0 = WD_14_0[0]; WD1 = WD_14_0[1]; WD2 = WD_14_0[2];
  //   WD3 = WD_14_0[3]; WD4 = WD_14_0[4]; WD5 = WD_14_0[5]; WD6 = WD_14_0[6]; WD7 = WD_14_0[7]; WD8 = WD_14_0[8];
  //   WD9 = WD_14_0[9]; WD10 = WD_14_0[10]; WD11 = WD_14_0[11]; WD12 = WD_14_0[12]; WD13 = WD_14_0[13];
  //   WD14 = WD_14_0[14]
endmodule
