// Digital circuit 1_bit_adder.dig as structural Verilog
module _1_bit_adder (
  input  X,
  input  Y,
  input  Cin,
  output S,
  output C
);

  wire and_1_out, and_2_out, xor_2_out;

  or or_1 (C, and_2_out, and_1_out);
  and and_1 (and_1_out, Cin, xor_2_out);
  xor xor_1 (S, Cin, xor_2_out);
  xor xor_2 (xor_2_out, Y, X);
  and and_2 (and_2_out, Y, X);
endmodule
