// Digital circuit 3bitPC.dig as structural Verilog
module _3bitPC (
  input  CLK,
  input  [2:0] I_2_0,
  output [2:0] O_2_0
);

  _1_bit_register _1_bit_register_1 (.Din(I_2_0[0]), .Sel(1'b1), .Clk(CLK), .Dout(O_2_0[0]));
  _1_bit_register _1_bit_register_2 (.Din(I_2_0[1]), .Sel(1'b1), .Clk(CLK), .Dout(O_2_0[1]));
  _1_bit_register _1_bit_register_3 (.Din(I_2_0[2]), .Sel(1'b1), .Clk(CLK), .Dout(O_2_0[2]));
endmodule
