// Digital circuit 4_bit_adder.dig as structural Verilog
module _4_bit_adder (
  input  A0,
  input  B0,
  input  A1,
  input  B1,
  input  A2,
  input  B2,
  input  A3,
  input  B3,
  input  C0,
  output S0,
  output S1,
  output S2,
  output S3
);

  wire _1_bit_adder_1_c, _1_bit_adder_3_c;

  _1_bit_adder _1_bit_adder_1 (.X(A0), .Y(B0), .Cin(C0), .S(S0), .C(_1_bit_adder_1_c));
  _1_bit_adder _1_bit_adder_2 (.X(A1), .Y(B1), .Cin(_1_bit_adder_1_c), .S(S1), .C(S1));
  _1_bit_adder _1_bit_adder_3 (.X(A2), .Y(B2), .Cin(S1), .S(S2), .C(_1_bit_adder_3_c));
  _1_bit_adder _1_bit_adder_4 (.X(A3), .Y(B3), .Cin(_1_bit_adder_3_c), .S(S3));  // open: C
endmodule
