// Digital circuit 4_bit_register.dig as structural Verilog
module _4_bit_register (
  input  clk,
  input  sel,
  input  [3:0] Din_3_0,
  output [3:0] Dout_3_0
);

  _1_bit_register _1_bit_register_1 (.Din(Din_3_0[3]), .Sel(sel), .Clk(clk), .Dout(Dout_3_0[0]));
  _1_bit_register _1_bit_register_2 (.Din(Din_3_0[2]), .Sel(sel), .Clk(clk), .Dout(Dout_3_0[1]));
  _1_bit_register _1_bit_register_3 (.Din(Din_3_0[1]), .Sel(sel), .Clk(clk), .Dout(Dout_3_0[2]));
  _1_bit_register _1_bit_register_4 (.Din(Din_3_0[0]), .Sel(sel), .Clk(clk), .Dout(Dout_3_0[3]));
endmodule
