// Digital circuit 8X15 SRAM.dig as structural Verilog
module _8X15_SRAM (
  input  [2:0] RA1_2_0,
  input  [2:0] RA2_2_0,
  input  [2:0] WA_2_0,
  input  WE,
  input  CLK,
  input  [14:0] WD_14_0,
  output [14:0] RD1_14_0,
  output [14:0] RD2_14_0
);

  wire RAi0, RAi1, RAi2, RAi3, RAi4, RAi5, RAi6, RAi7, RAii0, RAii1, RAii2, RAii3, RAii4, RAii5, RAii6,
       RAii7, W0, W1, W2, W3, W4, W5, W6, W7, WA0, WA1, WA2, WA3, WA4, WA5, WA6, WA7;
  wire [14:0] RDi0, RDi1, RDi2, RDi3, RDi4, RDi5, RDi6, RDi7, RDii0, RDii1, RDii2, RDii3, RDii4, RDii5,
       RDii6, RDii7;

  Decoder #(.Selector_Bits(3)) decoder_1 (
    .sel(WA_2_0), .out_0(WA0), .out_1(WA1), .out_2(WA2), .out_3(WA3), .out_4(WA4), .out_5(WA5), .out_6(WA6),
    .out_7(WA7));
  Decoder #(.Selector_Bits(3)) decoder_2 (
    .sel(RA1_2_0), .out_0(RAi0), .out_1(RAi1), .out_2(RAi2), .out_3(RAi3), .out_4(RAi4), .out_5(RAi5),
    .out_6(RAi6), .out_7(RAi7));
  Decoder #(.Selector_Bits(3)) decoder_3 (
    .sel(RA2_2_0), .out_0(RAii0), .out_1(RAii1), .out_2(RAii2), .out_3(RAii3), .out_4(RAii4), .out_5(RAii5),
    .out_6(RAii6), .out_7(RAii7));
  and and_1 (W0, WA0, WE);
  and and_2 (W1, WA1, WE);
  and and_3 (W2, WA2, WE);
  and and_4 (W3, WA3, WE);
  and and_5 (W4, WA4, WE);
  and and_6 (W5, WA5, WE);
  and and_7 (W6, WA6, WE);
  and and_8 (W7, WA7, WE);
  _1X15_SRAM _1x15_sram_1 (
    .RS1(RAi0), .RS2(RAii0), .WS(W0), .WD_14_0(WD_14_0), .CLK(CLK), .RD1_14_0(RDi0), .RD2_14_0(RDii0));
  _1X15_SRAM _1x15_sram_2 (
    .RS1(RAi3), .RS2(RAii3), .WS(W3), .WD_14_0(WD_14_0), .CLK(CLK), .RD1_14_0(RDi3), .RD2_14_0(RDii3));
  _1X15_SRAM _1x15_sram_3 (
    .RS1(RAi6), .RS2(RAii6), .WS(W6), .WD_14_0(WD_14_0), .CLK(CLK), .RD1_14_0(RDi6), .RD2_14_0(RDii6));
  _1X15_SRAM _1x15_sram_4 (
    .RS1(RAi1), .RS2(RAii1), .WS(W1), .WD_14_0(WD_14_0), .CLK(CLK), .RD1_14_0(RDi1), .RD2_14_0(RDii1));
  _1X15_SRAM _1x15_sram_5 (
    .RS1(RAi4), .RS2(RAii4), .WS(W4), .WD_14_0(WD_14_0), .CLK(CLK), .RD1_14_0(RDi4), .RD2_14_0(RDii4));
  _1X15_SRAM _1x15_sram_6 (
    .RS1(RAi7), .RS2(RAii7), .WS(W7), .WD_14_0(WD_14_0), .CLK(CLK), .RD1_14_0(RDi7), .RD2_14_0(RDii7));
  _1X15_SRAM _1x15_sram_7 (
    .RS1(RAi2), .RS2(RAii2), .WS(W2), .WD_14_0(WD_14_0), .CLK(CLK), .RD1_14_0(RDi2), .RD2_14_0(RDii2));
  _1X15_SRAM _1x15_sram_8 (
    .RS1(RAi5), .RS2(RAii5), .WS(W5), .WD_14_0(WD_14_0), .CLK(CLK), .RD1_14_0(RDi5), .RD2_14_0(RDii5));
  assign RD1_14_0 = RDi0 | RDi1 | RDi2 | RDi3 | RDi4 | RDi5 | RDi6 | RDi7;  // Or or_1, 15 bits wide
  assign RD2_14_0 = RDii0 | RDii1 | RDii2 | RDii3 | RDii4 | RDii5 | RDii6 | RDii7;  // Or or_2, 15 bits wide

  // Other names for the same wires on the sheet: WD[14:0] = WD_14_0
endmodule
