// Digital circuit ALU.dig as structural Verilog
module ALU (
  input  [1:0] Op_1_0,
  input  [3:0] A_3_0,
  input  [3:0] B_3_0,
  output [3:0] R_3_0,
  output ZF
);

  wire [3:0] adder_1_p4, shl_1_o, xor_1_o_3_0;

  XOR xor_1 (.A_3_0(A_3_0), .B_3_0(B_3_0), .O_3_0(xor_1_o_3_0));
  SHL shl_1 (.A_3_0(A_3_0), .B_3_0(B_3_0), .O(shl_1_o));
  // Adder adder_1: pin names not known; wires that end beside it: A_3_0, B_3_0, 1'b0, adder_1_p4
  Multiplexer #(.Selector_Bits(2), .Bits(4)) multiplexer_1 (
    .sel(Op_1_0), .in_0(xor_1_o_3_0), .in_1(shl_1_o), .in_2(adder_1_p4), .in_3(adder_1_p4), .out(R_3_0));
  nor nor_1 (ZF, R_3_0[0], R_3_0[1], R_3_0[2], R_3_0[3]);
endmodule
