// Digital circuit Control_unit.dig as structural Verilog
module Control_unit (
  input  [3:0] Opcode_3_0,
  input  ZF,
  output Immsel,
  output RegEN,
  output [1:0] Op_1_0,
  output JMPsel
);

  wire and_1_out, and_3_out, and_4_out, and_5_out, or_1_out, or_2_out;

  and and_1 (and_1_out, Opcode_3_0[2], Opcode_3_0[3]);
  and and_2 (Immsel, Opcode_3_0[2], ~Opcode_3_0[3]);  // And
  and and_3 (and_3_out, ~Opcode_3_0[2], ~Opcode_3_0[3]);  // And
  and and_4 (and_4_out, ~Opcode_3_0[0], ~Opcode_3_0[1]);  // And
  and and_5 (and_5_out, Opcode_3_0[0], ~Opcode_3_0[1], ZF);  // And
  or or_1 (or_1_out, Immsel, and_3_out);
  or or_2 (or_2_out, and_4_out, and_5_out);
  nor nor_1 (RegEN, and_1_out, or_1_out);
  and and_6 (JMPsel, and_1_out, or_2_out);

  assign Op_1_0 = Opcode_3_0[1:0];
endmodule
