// Digital circuit Final_CPU.dig as structural Verilog
module Final_CPU (
  input  [2:0] RA2_2_0,
  input  [2:0] WA_2_0,
  input  [2:0] WD_14_0,
  input  WE,
  input  CLK,
  input  PCE,
  output [3:0] R_3_0,
  output [2:0] Jump_address,
  output [14:0] RD2_14_0,
  output [1:0] R1_1_0,
  output [1:0] R2_1_0,
  output [2:0] Value_2_0,
  output [3:0] A_3_0,
  output [3:0] B_3_0,
  output [1:0] Op_1_0
);

  wire CPU_CLK, Immsel, JMP_SEL, RegEN, ZF;
  wire [2:0] _3bitpc_1_o_2_0, _3bitpcadder_1_o_2_0, multiplexer_1_out;
  wire [3:0] multiplexer_2_out;
  wire [11:0] _8x15_sram_1_p7;

  Multiplexer #(.Bits(3)) multiplexer_1 (
    .sel(JMP_SEL), .in_0(_3bitpcadder_1_o_2_0), .in_1(Jump_address), .out(multiplexer_1_out));
  _3bitPC _3bitpc_1 (.I_2_0(multiplexer_1_out), .CLK(CPU_CLK), .O_2_0(_3bitpc_1_o_2_0));
  and and_1 (CPU_CLK, PCE, CLK);
  _3bitPCADDER _3bitpcadder_1 (.O_2_0(_3bitpcadder_1_o_2_0), .I_2_0(_3bitpc_1_o_2_0));
  // _8X15_SRAM _8x15_sram_1: pin names not known; wires that end beside it: _3bitpc_1_o_2_0, RA2_2_0, WA_2_0, WE, CLK, WD_14_0, {Jump_address, _8x15_sram_1_p7[11], R1_1_0, R2_1_0, Value_2_0[0], _8x15_sram_1_p7[5:0]}, RD2_14_0
  Control_unit control_unit_1 (
    .Opcode_3_0({Jump_address, _8x15_sram_1_p7[11]}), .ZF(ZF), .Immsel(Immsel), .RegEN(RegEN),
    .Op_1_0(Op_1_0), .JMPsel(JMP_SEL));
  Register_set register_set_1 (
    .Wr_1_0(R1_1_0), .CLK(CPU_CLK), .RegEN(RegEN), .Wrd_3_0(R_3_0), .Ra_1_0(R1_1_0), .Rb_1_0(R2_1_0),
    .A_3_0(A_3_0), .B_3_0(B_3_0));
  ALU alu_1 (.Op_1_0(Op_1_0), .R_3_0(R_3_0), .A_3_0(A_3_0), .B_3_0(multiplexer_2_out), .ZF(ZF));
  Multiplexer #(.Bits(4)) multiplexer_2 (
    .sel(Immsel), .in_0(B_3_0), .in_1({1'b0, R2_1_0, Value_2_0[0]}), .out(multiplexer_2_out));

  assign Value_2_0[2:1] = R2_1_0;

  // Other names for the same wires on the sheet: Val[2:0] = {R2_1_0, Value_2_0[0]}; R2[1:0] = R2_1_0;
  //   R1[1:0] = R1_1_0; JMP_ADD[2:0] = Jump_address; Op[1:0] = Op_1_0; RA2[2:0] = RA2_2_0; RD2[14:0] = RD2_14_0;
  //   WA[2:0] = WA_2_0; WD[2:0] = WD_14_0
endmodule
