// Digital circuit SEA.dig as structural Verilog
module SEA (
  input  [3:0] in_1,
  input  [3:0] in_2
);

  _1X1_SRAM _1x1_sram_1 ();  // open: WD, WS, Clk, RS1, RS2, RD1, RD2
  _1X1_SRAM _1x1_sram_2 ();  // open: WD, WS, Clk, RS1, RS2, RD1, RD2
  _1X1_SRAM _1x1_sram_3 ();  // open: WD, WS, Clk, RS1, RS2, RD1, RD2
  _1X1_SRAM _1x1_sram_4 ();  // open: WD, WS, Clk, RS1, RS2, RD1, RD2
  _1X1_SRAM _1x1_sram_5 ();  // open: WD, WS, Clk, RS1, RS2, RD1, RD2
  _1X1_SRAM _1x1_sram_6 ();  // open: WD, WS, Clk, RS1, RS2, RD1, RD2
  _1X1_SRAM _1x1_sram_7 ();  // open: WD, WS, Clk, RS1, RS2, RD1, RD2
  _1X1_SRAM _1x1_sram_8 ();  // open: WD, WS, Clk, RS1, RS2, RD1, RD2
  // Pins of 1 and 4 bits meet at in_1
  // Pins of 1 and 4 bits meet at in_2

  // Other names for the same wires on the sheet: RAi0 = in_1[0]; RAi1 = in_1[1]; RAi2 = in_1[2]; RAi3 = in_1[3];
  //   RAii0 = in_2[0]; RAii1 = in_2[1]; RAii2 = in_2[2]; RAii3 = in_2[3]
endmodule
