// Digital circuit SHL.dig as structural Verilog
module SHL (
  input  [3:0] A_3_0,
  input  [3:0] B_3_0,
  output [3:0] O
);

  Multiplexer #(.Selector_Bits(2)) multiplexer_1 (
    .sel(B_3_0[1:0]), .in_0(A_3_0[3]), .in_1(A_3_0[2]), .in_2(A_3_0[1]), .in_3(A_3_0[0]), .out(O[3]));
  Multiplexer #(.Selector_Bits(2)) multiplexer_2 (
    .sel(B_3_0[1:0]), .in_0(1'b0), .in_1(A_3_0[3]), .in_2(A_3_0[2]), .in_3(A_3_0[1]), .out(O[2]));
  Multiplexer #(.Selector_Bits(2)) multiplexer_3 (
    .sel(B_3_0[1:0]), .in_0(1'b0), .in_1(1'b0), .in_2(A_3_0[1]), .in_3(A_3_0[2]), .out(O[1]));
  Multiplexer #(.Selector_Bits(2)) multiplexer_4 (
    .sel(B_3_0[1:0]), .in_0(1'b0), .in_1(1'b0), .in_2(1'b0), .in_3(A_3_0[0]), .out(O[0]));

  // Other names for the same wires on the sheet: A3 = A_3_0[0]; A2 = A_3_0[1]; A1 = A_3_0[2]; A0 = A_3_0[3]
endmodule
