// Digital circuit XOR.dig as structural Verilog
module XOR (
  input  [3:0] A_3_0,
  input  [3:0] B_3_0,
  output [3:0] O_3_0
);

  xor xor_1 (O_3_0[0], A_3_0[0], A_3_0[3]);
  xor xor_2 (O_3_0[1], A_3_0[1], B_3_0[1]);
  xor xor_3 (O_3_0[2], A_3_0[3], B_3_0[2]);
  xor xor_4 (O_3_0[3], A_3_0[3], A_3_0[3]);

  assign A_3_0[2] = A_3_0[3];
  assign {B_3_0[3], B_3_0[0]} = {2{A_3_0[3]}};
endmodule
