// Digital circuit register set.dig as structural Verilog
module register_set (
  input  [3:0] Wrd_3_0,
  input  CLK
);

  wire [3:0] _4_bit_register_1_dout_3_0, _4_bit_register_2_dout_3_0, _4_bit_register_3_dout_3_0, A, B;

  _4_bit_register _4_bit_register_1 (.Din_3_0(Wrd_3_0), .clk(CLK), .Dout_3_0(_4_bit_register_1_dout_3_0));  // open: sel
  _4_bit_register _4_bit_register_2 (.Din_3_0(Wrd_3_0), .clk(CLK), .Dout_3_0(_4_bit_register_2_dout_3_0));  // open: sel
  _4_bit_register _4_bit_register_3 (.Din_3_0(Wrd_3_0), .clk(CLK), .Dout_3_0(_4_bit_register_3_dout_3_0));  // open: sel
  Multiplexer #(.Selector_Bits(2), .Bits(4)) multiplexer_1 (
    .in_0(_4_bit_register_1_dout_3_0), .in_1(_4_bit_register_2_dout_3_0), .in_2(_4_bit_register_3_dout_3_0),
    .in_3(_4_bit_register_3_dout_3_0), .out(A));  // open: sel
  Multiplexer #(.Selector_Bits(2), .Bits(4)) multiplexer_2 (
    .in_0(_4_bit_register_1_dout_3_0), .in_1(_4_bit_register_2_dout_3_0), .in_2(_4_bit_register_3_dout_3_0),
    .in_3(_4_bit_register_3_dout_3_0), .out(B));  // open: sel
endmodule
